# Fritzing sketch wro (saved by Fritzing 1.0.1rc)
breadboards: 1

parts:
  Pi_5_8GB = Raspberry Pi 5
  Arduino_Nano_R4 = Arduino Nano R4
  MPU6050 = MPU-6050 Board GY-521 [form="♀ (female)" package=THT]
  Li-Po_2-cell_7_4V_3000mAh = LIPO-2200mAh
  Pi_Camera_Module_3 = Rasberry Pi NIOR Camera [chip_label=IC package="DIP (Dual Inline) [THT]"]  # not connected
  U1 = LM2596 step down module
  JGB37-520_1500_RPM = DC Motor with two-phase hall-encoder [part_number=VT-E-G25A-06-177E]
  DRV8874 = Adafruit DRV8871 [part_number="Adafruit #3190"]
  MG90S = Basic Servo
  HC-SR04_Front = HC-SR04 Ultrasonic Distance Sensor
  HC-SR04_Left = HC-SR04 Ultrasonic Distance Sensor
  HC-SR04_Right = HC-SR04 Ultrasonic Distance Sensor

nets:
  GND: Pi_5_8GB.PWR-1, Li-Po_2-cell_7_4V_3000mAh.-, U1.IN-, U1.OUT-, JGB37-520_1500_RPM.pin2, DRV8874.GND, MG90S.gnd, HC-SR04_Front.GND, HC-SR04_Left.GND, HC-SR04_Right.GND
  N1: Pi_5_8GB.PWR-2, Li-Po_2-cell_7_4V_3000mAh.+, U1.IN+, DRV8874.VMOTOR
  N2: Pi_5_8GB.UART_TX, Arduino_Nano_R4.Pin_23
  N3: Pi_5_8GB.UART_RX, Arduino_Nano_R4.Pin_24
  N4: Arduino_Nano_R4.Pin_12, MPU6050.pin1
  N5: Arduino_Nano_R4.Pin_14, Arduino_Nano_R4.Pin_21, MPU6050.pin2
  N6: Arduino_Nano_R4.Pin_17, Arduino_Nano_R4.Pin_18, MPU6050.pin4
  N7: Arduino_Nano_R4.Pin_19, MPU6050.pin3
  N8: Arduino_Nano_R4.Pin_27, HC-SR04_Left.ECHO
  N9: Arduino_Nano_R4.Pin_28, HC-SR04_Left.TRIG
  N10: Arduino_Nano_R4.Pin_29, HC-SR04_Front.ECHO
  N11: Arduino_Nano_R4.Pin_30, HC-SR04_Front.TRIG
  N12: Arduino_Nano_R4.Pin_31, MG90S.pulse
  N13: Arduino_Nano_R4.Pin_32, JGB37-520_1500_RPM.pin4
  N14: Arduino_Nano_R4.Pin_33, JGB37-520_1500_RPM.pin3
  N15: Arduino_Nano_R4.Pin_34, DRV8874.IN1
  N16: Arduino_Nano_R4.Pin_35, DRV8874.IN2
  N17: Arduino_Nano_R4.Pin_36, HC-SR04_Right.ECHO
  N18: Arduino_Nano_R4.Pin_37, HC-SR04_Right.TRIG
  VCC: U1.OUT+, JGB37-520_1500_RPM.pin5, MG90S.vcc, HC-SR04_Front.VCC, HC-SR04_Left.VCC, HC-SR04_Right.VCC
  N19: JGB37-520_1500_RPM.pin1, DRV8874.OUT1
  N20: JGB37-520_1500_RPM.pin6, DRV8874.OUT2

custom parts:
  Raspberry Pi 5: The RPi5, a faster version of the awesome Raspberry Pi4B ARM Board with 40 pin gpio.
  Arduino Nano R4: The Arduino Nano R4 without headers brings the robust performance of the RA4M1 microcontroller into the beloved Nano form factor, offering a compact and production-ready solution for embedded development, industrial automation, and custom hardware design.
  MPU-6050 Board GY-521: Acelerometro y Giroscopio MPU-6050 Board GY-521
  LIPO-2200mAh: 2200mAh Lipo-battery
  Rasberry Pi NIOR Camera: Camera
  LM2596 step down module: LM2596 DC-DC step down power supply module 3 A.
  Adafruit DRV8871: Crank up your robotics with powerful Adafruit DRV8871 motor driver breakout board. This motor driver has a lot of great specs that make it useful for a wide variety of mechatronics. In particular, the simple resistor-set current limiting and auto-magic PWM support make it super easy to use. Check out the specs for the DRV8871: 6.5V to 45V motor power voltage Up to 5.5V logic level on IN pins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
